# Fritzing sketch metrenumerique (saved by Fritzing 0.9.3b)
breadboards: 1

parts:
  LED1 = 7-SEGMENT-4DIGIT-YOUNGSUN [package=7-segment-4digit-youngsun-longpads]
  Composant1 = Arduino Uno (Rev3)
  R5 = Resistor [tolerance=±5% resistance=220 package=THT]
  R6 = Resistor [tolerance=±5% resistance=220 package=THT]
  R7 = Resistor [tolerance=±5% resistance=220 package=THT]
  R8 = Resistor [tolerance=±5% resistance=220 package=THT]
  hc-sr1 = hc-sr04

nets:
  N1: LED1.E, Composant1.D6_PWM
  N2: LED1.D, Composant1.D5_PWM
  N3: LED1.C, Composant1.D4
  N4: LED1.G, Composant1.D8
  N5: LED1.4, R5.Pin_1
  N6: LED1.3, R8.Pin_1
  N7: LED1.2, R7.Pin_1
  N8: LED1.F, Composant1.D7
  N9: LED1.A, Composant1.D2
  N10: LED1.1, R6.Pin_1
  N11: Composant1.A0, R6.Pin_0
  N12: Composant1.A1, R7.Pin_0
  N13: Composant1.A2, R8.Pin_0
  N14: Composant1.A3, R5.Pin_0
  N15: Composant1.D10_PWM/SS, hc-sr1.Echo
  N16: Composant1.D11_PWM/MOSI, hc-sr1.Trig
  5V: Composant1.5V, hc-sr1.VCC
  GND: Composant1.GND, hc-sr1.GND

custom parts:
  7-SEGMENT-4DIGIT-YOUNGSUN: This is a part for the 4-Digit 7-segment LEDs from Young Sun. Different from the Digikey LEDs, all 16 pins are used. The LONGPADS Variant is used for a test jig, but you may like it because there is more pad to solder to. If you are concerned about routing space, the standard works just fine though.

// code stored in the sketch: Display4Digit7Segments.cpp
#include <Arduino.h>
#include "Display4Digit7Segments.h"

Display4Digit7Segments::Display4Digit7Segments(int segmentIdBase, int digitIdBase)
{
  mSegmentId = segmentIdBase;
  mDigitId = digitIdBase;
}

void Display4Digit7Segments::InitializeOutputs()
{
  // configure outputs
  for (int i = 0; i < 7; i++) {
    pinMode(mSegmentId + i, OUTPUT);
  }

  for (int i = 0; i < 4; i++) {
    pinMode(mDigitId + i, OUTPUT);
  }
}

void Display4Digit7Segments::Display(int value)
{
  Display(value, MaxDigit);
}

void Display4Digit7Segments::Display(int value, int nbDigitToDisplay)
{
  if (nbDigitToDisplay < 1) {
    nbDigitToDisplay = 1;
  }
  if (nbDigitToDisplay > MaxDigit) {
    nbDigitToDisplay = MaxDigit;
  }
  
  GetDigits(value);
  DisplayDigits(nbDigitToDisplay);
}

void Display4Digit7Segments::GetDigits(int value)
{
  mDigits[0] = value / 1000;
  mDigits[0] = mDigits[0] % 10;
  value = value - (mDigits[0] * 1000);
  mDigits[1] = value / 100;
  value = value - (mDigits[1] * 100);
  mDigits[2] = value / 10;
  mDigits[3] = value - (mDigits[2] * 10);
}

void Display4Digit7Segments::DisplayDigits(int nbDigitToDisplay)
{
  for (int i = 0; i < 4; i++) {
    digitalWrite( mDigitId + i, LOW);
  }

  for (int i = 4 - nbDigitToDisplay; i < 4; i++) {
    digitalWrite( mDigitId + i, HIGH);
    DisplayDigit(mDigits[i]);
    delay(DTime);
    digitalWrite( mDigitId + i, LOW);
  }

  delay(DTime);
}

void Display4Digit7Segments::DisplayDigit(int digitValue)
{
  for (int i = 0; i < 7; i++) {
    digitalWrite( mSegmentId + i, Segments[digitValue][i]);
  }
}

// code stored in the sketch: Display4Digit7Segments.h
/*
  Ultrasonic.h - Library for HC-SR04 Ultrasonic Ranging Module.library

*/

#ifndef Display4Digit7Segments_h
#define Display4Digit7Segments_h

#include <Arduino.h>

#define SEGMENT_OFF 10
#define SEGMENT_UNKNOW 11


class Display4Digit7Segments
{
  public:
    Display4Digit7Segments(int segmentIdBase, int digitIdBase);
    void InitializeOutputs();
    void Display(int value);
    void Display(int value, int nbDigitToDisplay);

  private:
    int mSegmentId;
    int mDigitId;
    int mDigits[5];
    unsigned long mPreviousMillis = 0; 
    const int MaxDigit = 4;
    const int DTime = 4;
    const byte Segments[12][8] = {
      // A     B     C     D     E     F     G
      { LOW,  LOW,  LOW,  LOW,  LOW,  LOW,  HIGH }, // 0
      { HIGH, LOW,  LOW,  HIGH, HIGH, HIGH, HIGH }, // 1
      { LOW,  LOW,  HIGH, LOW,  LOW,  HIGH, LOW }, // 2
      { LOW,  LOW,  LOW,  LOW,  HIGH, HIGH, LOW }, // 3
      { HIGH, LOW,  LOW,  HIGH, HIGH, LOW,  LOW }, // 4
      { LOW,  HIGH, LOW,  LOW,  HIGH, LOW,  LOW }, // 5
      { LOW,  HIGH, LOW,  LOW,  LOW,  LOW,  LOW }, // 6
      { LOW,  LOW,  LOW,  HIGH, HIGH, HIGH, HIGH  }, // 7
      { LOW,  LOW,  LOW,  LOW,  LOW,  LOW,  LOW }, // 8
      { LOW,  LOW,  LOW,  LOW,  HIGH, LOW,  LOW }, // 9
      { HIGH, HIGH, HIGH, HIGH, HIGH, HIGH, HIGH },  // all off
      { HIGH, HIGH, HIGH, HIGH, HIGH, HIGH, LOW }  // -
    };

    void GetDigits(int value);
    void DisplayDigits(int nbDigitToDisplay);
    void DisplayDigit(int digitValue);
};

#endif

// code stored in the sketch: metrenumerique.ino

#include "Ultrasonic.h"
#include "Display4Digit7Segments.h"

int aPin = 2;  //         A
int bPin = 3;  //      ________
int cPin = 4;  //     |        |
int dPin = 5;  //   F |        |  B
int ePin = 6;  //     |    G   |
int fPin = 7;  //     |________|
int gPin = 8;  //     |        |
int GND1 = 14; //     |        |
int GND2 = 15; //   E |        |   C
int GND3 = 16; //     |________|
int GND4 = 17; //
int num;       //         D
int dig1;
int dig2 = 0;
int dig3 = 0;
int dig4 = 0;
int dotDigit = 9;
int DTime = 4;

int sensorTrigPlotId = 11;
int sensorEchoPlotId = 10;
Ultrasonic ultrasonic(sensorTrigPlotId, sensorEchoPlotId); //(Trig,Echo)
Display4Digit7Segments display4Digits7Segments(aPin, GND1);

const long interval = 1000;
unsigned long previousMillis = 0;        // will store last time LED was updated
int mDistanceInCm =0;
void setup()
{
  display4Digits7Segments.InitializeOutputs();

  pinMode(dotDigit, OUTPUT);
  //Serial.begin(9600);
}
void loop()
{
  unsigned long currentMillis = millis();
  if (currentMillis - previousMillis >= interval) {
    // save the last time you blinked the LED
    previousMillis = currentMillis;

    mDistanceInCm = ultrasonic.Ranging(CM);
  }
  display4Digits7Segments.Display(mDistanceInCm, 3);
  delay(DTime);
}

// code stored in the sketch: ultrasonic.cpp
/*
  Ultrasonic.cpp - Library for HC-SR04 Ultrasonic Ranging Module.library

*/

#include <Arduino.h>
#include "Ultrasonic.h"

Ultrasonic::Ultrasonic(int TP, int EP)
{
   pinMode(TP,OUTPUT);
   pinMode(EP,INPUT);
   Trig_pin=TP;
   Echo_pin=EP;
}

long Ultrasonic::Timing()
{
  digitalWrite(Trig_pin, LOW);
  delayMicroseconds(2);
  digitalWrite(Trig_pin, HIGH);
  delayMicroseconds(10);
  digitalWrite(Trig_pin, LOW);
  duration = pulseIn(Echo_pin,HIGH);
  return duration;
}

long Ultrasonic::Ranging(int sys)
{
  Timing();
  distacne_cm = duration /29 / 2 ;
  distance_inc = duration / 74 / 2;
  if (sys)
  return distacne_cm;
  else
  return distance_inc;
}

// code stored in the sketch: Ultrasonic.h
/*
  Ultrasonic.h - Library for HC-SR04 Ultrasonic Ranging Module.library

*/

#ifndef Ultrasonic_h
#define Ultrasonic_h

#include <Arduino.h>

#define CM 1
#define INC 0


class Ultrasonic
{
  public:
    Ultrasonic(int TP, int EP);
    long Timing();
    long Ranging(int sys);

    private:
    int Trig_pin;
    int Echo_pin;
    long  duration,distacne_cm,distance_inc;
    
};

#endif
